// Logisim project CircuitoCalculadorWithUla.circ as structural Verilog: 18 circuits, main circuit main
module main (
  input  [7:0] InserirValor,
  input  SelecionarValor,
  input  [1:0] SelecionarRA,
  input  [2:0] SelOp,
  input  [1:0] SelecionarRB,
  input  [1:0] SelecionarRW,
  output [7:0] out_7
);

  wire Escrever_out, ula_1_overflow, ula_1_z;
  wire [7:0] bancoregistradores_1_saidaa, bancoregistradores_1_saidab, mux8bits2x1_1_saida;

  Mux8Bits2x1 mux8bits2x1_1 (
    .EntradaA(out_7), .EntradaB(InserirValor), .Selecao(SelecionarValor), .Saida(mux8bits2x1_1_saida));
  Button Escrever (.out(Escrever_out));
  BancoRegistradores bancoregistradores_1 (
    .SelecionarA(SelecionarRA), .SelecionarB(SelecionarRB), .Escrever(Escrever_out),
    .SelecionarWR(SelecionarRW), .Entrada(mux8bits2x1_1_saida), .SaidaA(bancoregistradores_1_saidaa),
    .SaidaB(bancoregistradores_1_saidab));
  LED C (.in(ula_1_overflow));
  ULA ula_1 (
    .SelOps(SelOp), .EntradaA(bancoregistradores_1_saidaa), .EntradaB(bancoregistradores_1_saidab),
    .Overflow(ula_1_overflow), .Resultado(out_7), .Z(ula_1_z));
  LED Z (.in(ula_1_z));
  LED led_1 (.in(out_7[7]));
  LED led_2 (.in(out_7[6]));
  LED led_3 (.in(out_7[5]));
  LED led_4 (.in(out_7[4]));
  LED led_5 (.in(out_7[3]));
  LED led_6 (.in(out_7[2]));
  LED led_7 (.in(out_7[1]));
  LED led_8 (.in(out_7[0]));

  // Notes on the sheet:
  //   Multiplicar = 001
  //   somar = 010
endmodule

module AxorB (
  input  [7:0] A,
  input  [7:0] B,
  output [7:0] S
);

  assign S = A ^ B;  // XOR_Gate xor_1, 8 bits wide
endmodule

module AandB (
  input  [7:0] A,
  input  [7:0] B,
  output [7:0] S
);

  assign S = A & B;  // AND_Gate and_1, 8 bits wide
endmodule

module AnorB (
  input  [7:0] A,
  input  [7:0] B,
  output [7:0] S
);

  assign S = ~(A | B);  // NOR_Gate nor_1, 8 bits wide
endmodule

module Mux8x1 (
  input  [7:0] Entrada,
  input  [2:0] Selecao,
  output Saida
);

  wire not_1_out, not_2_out, not_3_out, or_1_out, or_2_out, or_3_out, or_4_out, or_5_out, or_6_out, or_7_out,
       or_8_out;

  not not_1 (not_1_out, Selecao[2]);
  not not_2 (not_2_out, Selecao[1]);
  not not_3 (not_3_out, Selecao[0]);
  or or_1 (or_1_out, Entrada[0], Selecao[2], Selecao[1], Selecao[0]);
  or or_2 (or_2_out, Entrada[1], Selecao[2], Selecao[1], not_3_out);
  or or_3 (or_3_out, Entrada[2], Selecao[2], not_2_out, Selecao[0]);
  or or_4 (or_4_out, Entrada[4], not_1_out, Selecao[1], Selecao[0]);
  or or_5 (or_5_out, Entrada[7], not_1_out, not_2_out, not_3_out);
  or or_6 (or_6_out, Entrada[3], Selecao[2], not_2_out, not_3_out);
  or or_7 (or_7_out, Entrada[5], not_1_out, Selecao[1], not_3_out);
  or or_8 (or_8_out, Entrada[6], not_1_out, not_2_out, Selecao[0]);
  and and_1 (Saida, or_1_out, or_2_out, or_3_out, or_4_out, or_5_out, or_6_out, or_7_out, or_8_out);
endmodule

module Registrador8Bits (
  input  [7:0] Entrada,
  input  Clock,
  output [7:0] Saida
);

  D_Flip_Flop d_ff_1 (.D(Entrada[0]), .clk(Clock), .Q(Saida[0]));  // open: Qn, preset, reset
  D_Flip_Flop d_ff_2 (.D(Entrada[1]), .clk(Clock), .Q(Saida[1]));  // open: Qn, preset, reset
  D_Flip_Flop d_ff_3 (.D(Entrada[2]), .clk(Clock), .Q(Saida[2]));  // open: Qn, preset, reset
  D_Flip_Flop d_ff_4 (.D(Entrada[3]), .clk(Clock), .Q(Saida[3]));  // open: Qn, preset, reset
  D_Flip_Flop d_ff_5 (.D(Entrada[4]), .clk(Clock), .Q(Saida[4]));  // open: Qn, preset, reset
  D_Flip_Flop d_ff_6 (.D(Entrada[5]), .clk(Clock), .Q(Saida[5]));  // open: Qn, preset, reset
  D_Flip_Flop d_ff_7 (.D(Entrada[6]), .clk(Clock), .Q(Saida[6]));  // open: Qn, preset, reset
  D_Flip_Flop d_ff_8 (.D(Entrada[7]), .clk(Clock), .Q(Saida[7]));  // open: Qn, preset, reset
endmodule

module Not8Bits (
  input  [7:0] Entrada,
  output [7:0] Saida
);

  assign Saida = ~Entrada;  // NOT_Gate not_1, 8 bits wide
endmodule

module ULA (
  input  [2:0] SelOps,
  input  [7:0] EntradaA,
  input  [7:0] EntradaB,
  output Overflow,
  output [7:0] Resultado,
  output Z
);

  wire verificarzero8x1_1_saida;
  wire [7:0] aandb_1_s, anorb_1_s, axorb_1_s, divider_1_out, divider_1_rem, multiplier_1_cout,
       multiplier_1_out, somadorsubtraidor_1_resultado, somadorsubtraidor_2_resultado;
  wire [7:1] not_1_out;

  Multiplier multiplier_1 (.a(EntradaA), .b(EntradaB), .out(multiplier_1_out), .cout(multiplier_1_cout));  // open: cin
  Divider divider_1 (.a(EntradaA), .b(EntradaB), .out(divider_1_out), .rem(divider_1_rem));  // open: upper
  AxorB axorb_1 (.A(EntradaA), .B(EntradaB), .S(axorb_1_s));
  SomadorSubtraidor somadorsubtraidor_1 (
    .EntradaA(EntradaA), .EntradaB(EntradaB), .Subtrair(1'b0), .Resultado(somadorsubtraidor_1_resultado),
    .Overflow(not_1_out[2]));
  AandB aandb_1 (.A(EntradaA), .B(EntradaB), .S(aandb_1_s));
  AnorB anorb_1 (.A(EntradaA), .B(EntradaB), .S(anorb_1_s));
  SomadorSubtraidor somadorsubtraidor_2 (
    .EntradaA(EntradaA), .EntradaB(EntradaB), .Subtrair(1'b1), .Resultado(somadorsubtraidor_2_resultado),
    .Overflow(not_1_out[7]));
  ExactlyOne xor_1 (
    .out(not_1_out[5]), .in0(divider_1_rem[0]), .in1(divider_1_rem[1]), .in2(divider_1_rem[2]),
    .in3(divider_1_rem[3]), .in4(divider_1_rem[4]), .in5(divider_1_rem[5]), .in6(divider_1_rem[6]),
    .in7(divider_1_rem[7]));
  Mux8bits8x1 mux8bits8x1_1 (
    .Selecao(SelOps), .Entrada0(aandb_1_s), .Entrada1(multiplier_1_out),
    .Entrada2(somadorsubtraidor_1_resultado), .Entrada3(anorb_1_s), .Entrada4(aandb_1_s),
    .Entrada5(divider_1_out), .Entrada6(axorb_1_s), .Entrada7(somadorsubtraidor_2_resultado),
    .out_10(Resultado));
  VerificarZero8x1 verificarzero8x1_1 (.Entrada(multiplier_1_cout), .Saida(verificarzero8x1_1_saida));
  not not_1 (not_1_out[1], verificarzero8x1_1_saida);
  Mux8x1 mux8x1_1 (
    .Entrada({not_1_out[7], 1'b0, not_1_out[5], 2'b00, not_1_out[2:1], 1'b0}), .Selecao(SelOps),
    .Saida(Overflow));
  VerificarZero8x1 verificarzero8x1_2 (.Entrada(Resultado), .Saida(Z));
endmodule

module SomadorUnitario (
  input  BitExtra,
  input  A,
  input  B,
  output S,
  output SResto
);

  wire and_1_out, and_2_out, and_3_out, xor_1_out;

  and and_1 (and_1_out, BitExtra, A);
  and and_2 (and_2_out, BitExtra, B);
  and and_3 (and_3_out, A, B);
  xor xor_1 (xor_1_out, A, B);
  or or_1 (SResto, and_1_out, and_2_out, and_3_out);
  xor xor_2 (S, xor_1_out, BitExtra);
endmodule

module SomadorSubtraidor (
  input  [7:0] EntradaA,
  input  [7:0] EntradaB,
  input  Subtrair,
  output [7:0] Resultado,
  output Overflow
);

  wire somadorunitario_1_sresto, somadorunitario_2_sresto, somadorunitario_3_sresto,
       somadorunitario_4_sresto, somadorunitario_5_sresto, somadorunitario_6_sresto,
       somadorunitario_7_sresto, somadorunitario_8_sresto, xor_1_out, xor_2_out, xor_3_out, xor_4_out,
       xor_5_out, xor_6_out, xor_7_out, xor_8_out;

  xor xor_1 (xor_1_out, Subtrair, EntradaB[0]);
  xor xor_2 (xor_2_out, Subtrair, EntradaB[1]);
  xor xor_3 (xor_3_out, Subtrair, EntradaB[2]);
  xor xor_4 (xor_4_out, Subtrair, EntradaB[3]);
  xor xor_5 (xor_5_out, Subtrair, EntradaB[4]);
  xor xor_6 (xor_6_out, Subtrair, EntradaB[5]);
  xor xor_7 (xor_7_out, Subtrair, EntradaB[6]);
  xor xor_8 (xor_8_out, Subtrair, EntradaB[7]);
  SomadorUnitario somadorunitario_1 (
    .BitExtra(Subtrair), .A(EntradaA[0]), .B(xor_1_out), .S(Resultado[0]), .SResto(somadorunitario_1_sresto));
  SomadorUnitario somadorunitario_2 (
    .BitExtra(somadorunitario_1_sresto), .A(EntradaA[1]), .B(xor_2_out), .S(Resultado[1]),
    .SResto(somadorunitario_2_sresto));
  SomadorUnitario somadorunitario_3 (
    .BitExtra(somadorunitario_2_sresto), .A(EntradaA[2]), .B(xor_3_out), .S(Resultado[2]),
    .SResto(somadorunitario_3_sresto));
  SomadorUnitario somadorunitario_4 (
    .BitExtra(somadorunitario_3_sresto), .A(EntradaA[3]), .B(xor_4_out), .S(Resultado[3]),
    .SResto(somadorunitario_4_sresto));
  SomadorUnitario somadorunitario_5 (
    .BitExtra(somadorunitario_4_sresto), .A(EntradaA[4]), .B(xor_5_out), .S(Resultado[4]),
    .SResto(somadorunitario_5_sresto));
  SomadorUnitario somadorunitario_6 (
    .BitExtra(somadorunitario_5_sresto), .A(EntradaA[5]), .B(xor_6_out), .S(Resultado[5]),
    .SResto(somadorunitario_6_sresto));
  SomadorUnitario somadorunitario_7 (
    .BitExtra(somadorunitario_6_sresto), .A(EntradaA[6]), .B(xor_7_out), .S(Resultado[6]),
    .SResto(somadorunitario_7_sresto));
  SomadorUnitario somadorunitario_8 (
    .BitExtra(somadorunitario_7_sresto), .A(EntradaA[7]), .B(xor_8_out), .S(Resultado[7]),
    .SResto(somadorunitario_8_sresto));
  xor xor_9 (Overflow, somadorunitario_8_sresto, somadorunitario_7_sresto);
endmodule

module BancoRegistradores (
  input  [1:0] SelecionarA,
  input  [1:0] SelecionarB,
  input  Escrever,
  input  [1:0] SelecionarWR,
  input  [7:0] Entrada,
  output [7:0] SaidaA,
  output [7:0] SaidaB
);

  wire demux2x1_1_saida0, demux2x1_1_saida1, demux2x1_1_saida2, demux2x1_1_saida3;
  wire [7:0] registrador8bits_1_saida, registrador8bits_2_saida, registrador8bits_3_saida,
       registrador8bits_4_saida;

  Demux2x1 demux2x1_1 (
    .Selecao(SelecionarWR), .Entrada(Escrever), .Saida0(demux2x1_1_saida0), .Saida1(demux2x1_1_saida1),
    .Saida2(demux2x1_1_saida2), .Saida3(demux2x1_1_saida3));
  Registrador8Bits registrador8bits_1 (.Entrada(Entrada), .Clock(demux2x1_1_saida0), .Saida(registrador8bits_1_saida));
  Registrador8Bits registrador8bits_2 (.Entrada(Entrada), .Clock(demux2x1_1_saida1), .Saida(registrador8bits_2_saida));
  Registrador8Bits registrador8bits_3 (.Entrada(Entrada), .Clock(demux2x1_1_saida2), .Saida(registrador8bits_3_saida));
  Registrador8Bits registrador8bits_4 (.Entrada(Entrada), .Clock(demux2x1_1_saida3), .Saida(registrador8bits_4_saida));
  Mux8bits4x1 mux8bits4x1_1 (
    .Entrada0(registrador8bits_1_saida), .Entrada1(registrador8bits_2_saida),
    .Entrada2(registrador8bits_3_saida), .Entrada3(registrador8bits_4_saida), .Selecao(SelecionarA),
    .Saida(SaidaA));
  Mux8bits4x1 mux8bits4x1_2 (
    .Entrada0(registrador8bits_1_saida), .Entrada1(registrador8bits_2_saida),
    .Entrada2(registrador8bits_3_saida), .Entrada3(registrador8bits_4_saida), .Selecao(SelecionarB),
    .Saida(SaidaB));
endmodule

module Demux2x1 (
  input  [1:0] Selecao,
  input  Entrada,
  output Saida0,
  output Saida1,
  output Saida2,
  output Saida3
);

  wire not_1_out, not_2_out;

  not not_1 (not_1_out, Selecao[1]);
  not not_2 (not_2_out, Selecao[0]);
  and and_1 (Saida0, not_1_out, not_2_out, Entrada);
  and and_2 (Saida1, not_1_out, Selecao[0], Entrada);
  and and_3 (Saida2, Selecao[1], not_2_out, Entrada);
  and and_4 (Saida3, Selecao[1], Selecao[0], Entrada);
endmodule

module Mux4x1 (
  input  [1:0] Selecao,
  input  [3:0] Entrada,
  output Saida
);

  wire and_1_out, and_2_out, and_3_out, and_4_out, not_1_out, not_2_out;

  not not_1 (not_1_out, Selecao[1]);
  not not_2 (not_2_out, Selecao[0]);
  and and_1 (and_1_out, not_1_out, not_2_out, Entrada[0]);
  and and_2 (and_2_out, not_1_out, Selecao[0], Entrada[1]);
  and and_3 (and_3_out, Selecao[1], not_2_out, Entrada[2]);
  and and_4 (and_4_out, Selecao[1], Selecao[0], Entrada[3]);
  or or_1 (Saida, and_1_out, and_2_out, and_3_out, and_4_out);
endmodule

module Mux2x1 (
  input  [1:0] Entrada,
  input  Selecao,
  output Saida
);

  wire and_1_out, and_2_out, not_1_out;

  not not_1 (not_1_out, Selecao);
  and and_1 (and_1_out, not_1_out, Entrada[0]);
  and and_2 (and_2_out, Selecao, Entrada[1]);
  or or_1 (Saida, and_1_out, and_2_out);
endmodule

module Mux8bits4x1 (
  input  [7:0] Entrada0,
  input  [7:0] Entrada1,
  input  [7:0] Entrada2,
  input  [7:0] Entrada3,
  input  [1:0] Selecao,
  output [7:0] Saida
);

  Mux4x1 mux4x1_1 (.Selecao(Selecao), .Entrada({Entrada3[0], Entrada2[0], Entrada1[0], Entrada0[0]}), .Saida(Saida[0]));
  Mux4x1 mux4x1_2 (.Selecao(Selecao), .Entrada({Entrada3[1], Entrada2[1], Entrada1[1], Entrada0[1]}), .Saida(Saida[1]));
  Mux4x1 mux4x1_3 (.Selecao(Selecao), .Entrada({Entrada3[2], Entrada2[2], Entrada1[2], Entrada0[2]}), .Saida(Saida[2]));
  Mux4x1 mux4x1_4 (.Selecao(Selecao), .Entrada({Entrada3[3], Entrada2[3], Entrada1[3], Entrada0[3]}), .Saida(Saida[3]));
  Mux4x1 mux4x1_5 (.Selecao(Selecao), .Entrada({Entrada3[4], Entrada2[4], Entrada1[4], Entrada0[4]}), .Saida(Saida[4]));
  Mux4x1 mux4x1_6 (.Selecao(Selecao), .Entrada({Entrada3[5], Entrada2[5], Entrada1[5], Entrada0[5]}), .Saida(Saida[5]));
  Mux4x1 mux4x1_7 (.Selecao(Selecao), .Entrada({Entrada3[6], Entrada2[6], Entrada1[6], Entrada0[6]}), .Saida(Saida[6]));
  Mux4x1 mux4x1_8 (.Selecao(Selecao), .Entrada({Entrada3[7], Entrada2[7], Entrada1[7], Entrada0[7]}), .Saida(Saida[7]));
endmodule

module Mux8bits8x1 (
  input  [2:0] Selecao,
  input  [7:0] Entrada0,
  input  [7:0] Entrada1,
  input  [7:0] Entrada2,
  input  [7:0] Entrada3,
  input  [7:0] Entrada4,
  input  [7:0] Entrada5,
  input  [7:0] Entrada6,
  input  [7:0] Entrada7,
  output [7:0] out_10
);

  Mux8x1 mux8x1_1 (
    .Entrada({Entrada7[7], Entrada6[7], Entrada5[7], Entrada4[7], Entrada3[7], Entrada2[7], Entrada1[7], Entrada0[7]}),
    .Selecao(Selecao), .Saida(out_10[7]));
  Mux8x1 mux8x1_2 (
    .Entrada({Entrada7[6], Entrada6[6], Entrada5[6], Entrada4[6], Entrada3[6], Entrada2[6], Entrada1[6], Entrada0[6]}),
    .Selecao(Selecao), .Saida(out_10[6]));
  Mux8x1 mux8x1_3 (
    .Entrada({Entrada7[5], Entrada6[5], Entrada5[5], Entrada4[5], Entrada3[5], Entrada2[5], Entrada1[5], Entrada0[5]}),
    .Selecao(Selecao), .Saida(out_10[5]));
  Mux8x1 mux8x1_4 (
    .Entrada({Entrada7[4], Entrada6[4], Entrada5[4], Entrada4[4], Entrada3[4], Entrada2[4], Entrada1[4], Entrada0[4]}),
    .Selecao(Selecao), .Saida(out_10[4]));
  Mux8x1 mux8x1_5 (
    .Entrada({Entrada7[3], Entrada6[3], Entrada5[3], Entrada4[3], Entrada3[3], Entrada2[3], Entrada1[3], Entrada0[3]}),
    .Selecao(Selecao), .Saida(out_10[3]));
  Mux8x1 mux8x1_6 (
    .Entrada({Entrada7[2], Entrada6[2], Entrada5[2], Entrada4[2], Entrada3[2], Entrada2[2], Entrada1[2], Entrada0[2]}),
    .Selecao(Selecao), .Saida(out_10[2]));
  Mux8x1 mux8x1_7 (
    .Entrada({Entrada7[1], Entrada6[1], Entrada5[1], Entrada4[1], Entrada3[1], Entrada2[1], Entrada1[1], Entrada0[1]}),
    .Selecao(Selecao), .Saida(out_10[1]));
  Mux8x1 mux8x1_8 (
    .Entrada({Entrada7[0], Entrada6[0], Entrada5[0], Entrada4[0], Entrada3[0], Entrada2[0], Entrada1[0], Entrada0[0]}),
    .Selecao(Selecao), .Saida(out_10[0]));
endmodule

module Mux8Bits2x1 (
  input  [7:0] EntradaA,
  input  [7:0] EntradaB,
  input  Selecao,
  output [7:0] Saida
);

  Mux2x1 mux2x1_1 (.Entrada({EntradaB[0], EntradaA[0]}), .Selecao(Selecao), .Saida(Saida[0]));
  Mux2x1 mux2x1_2 (.Entrada({EntradaB[1], EntradaA[1]}), .Selecao(Selecao), .Saida(Saida[1]));
  Mux2x1 mux2x1_3 (.Entrada({EntradaB[2], EntradaA[2]}), .Selecao(Selecao), .Saida(Saida[2]));
  Mux2x1 mux2x1_4 (.Entrada({EntradaB[3], EntradaA[3]}), .Selecao(Selecao), .Saida(Saida[3]));
  Mux2x1 mux2x1_5 (.Entrada({EntradaB[4], EntradaA[4]}), .Selecao(Selecao), .Saida(Saida[4]));
  Mux2x1 mux2x1_6 (.Entrada({EntradaB[5], EntradaA[5]}), .Selecao(Selecao), .Saida(Saida[5]));
  Mux2x1 mux2x1_7 (.Entrada({EntradaB[6], EntradaA[6]}), .Selecao(Selecao), .Saida(Saida[6]));
  Mux2x1 mux2x1_8 (.Entrada({EntradaB[7], EntradaA[7]}), .Selecao(Selecao), .Saida(Saida[7]));
endmodule

module VerificarZero8x1 (
  input  [7:0] Entrada,
  output Saida
);

  wire not_1_out, not_2_out, not_3_out, not_4_out, not_5_out, not_6_out, not_7_out, not_8_out;

  not not_1 (not_1_out, Entrada[7]);
  not not_2 (not_2_out, Entrada[6]);
  not not_3 (not_3_out, Entrada[5]);
  not not_4 (not_4_out, Entrada[4]);
  not not_5 (not_5_out, Entrada[3]);
  not not_6 (not_6_out, Entrada[2]);
  not not_7 (not_7_out, Entrada[1]);
  not not_8 (not_8_out, Entrada[0]);
  and and_1 (Saida, not_8_out, not_7_out, not_6_out, not_5_out, not_4_out, not_3_out, not_2_out, not_1_out);
endmodule
